# Fritzing sketch circuit layout (saved by Fritzing 0.9.9b)
circuit board: 4.04061cm x 2.30741cm
breadboards: 1

parts:
  J2 = female pin header, 3 pins [form="♀ (female)"]  # not connected
  J3 = female pin header, 3 pins [form="♀ (female)"]
  R2 = Resistor [tolerance=±5% power=0.25 resistance=10k package=THT]
  R1 = Resistor [tolerance=±5% power=0.25 resistance=10k package=THT]
  C1 = Tantalum Capacitor [capacitance=0.1µF voltage=35V package="100 mil [THT, tantalum]"]
  C2 = Tantalum Capacitor [capacitance=10µF voltage=35V package="200 mil [THT, tantalum]"]
  J1 = female pin header, 4 pins [form="♀ (female)"]
  J2_2 = female pin header, 4 pins [form="♀ (female)"]
  IC1 = IC, DIP package, 6 pins [chip_label=MCP3221]

nets:
  SIG: J3.pin1, IC1.pin3
  EMG-/GND: J3.pin2, C1.-, C2.-, J1.pin2, J2_2.pin2, IC1.pin2
  EMG+/VCC: J3.pin3, R2.Pin_0, R1.Pin_0, C1.+, C2.+, J1.pin1, J2_2.pin1, IC1.pin1
  SDA: R2.Pin_1, J1.pin3, J2_2.pin3, IC1.pin4
  SCL: R1.Pin_1, J1.pin4, J2_2.pin4, IC1.pin6
